# Fritzing sketch Schema-initiala (saved by Fritzing 0.9.3b)

parts:
  M2 = DC Motor
  VCC1 = Battery block 9V
  VCC2 = 4 x AAA Battery Mount
  Grove1 = Grove Light Sensor
  M1 = DC Motor
  J1 = Basic Servo
  hc-sr1 = hc-sr04
  Parte1 = Arduino Uno (Rev3) - ICSP
  S1 = H-Bridge with L298N
  R9 = Resistor [tolerance=±5% resistance=220 package=THT]
  R10 = Resistor [tolerance=±5% resistance=220 package=THT]
  U3 = ESP8266 WiFi Module [part_number=ESP8266]

nets:
  N1: M2.pin_1, S1.M2-01
  N2: M2.pin_2, S1.M2-02
  N3: VCC1.-, S1.GND
  N4: VCC1.+, S1.12V
  GND: VCC2.-, Grove1.GND, hc-sr1.GND
  VCC: VCC2.+, Grove1.VCC, hc-sr1.VCC
  N5: Grove1.SIG, Parte1.A2
  N6: M1.pin_1, S1.M1-02
  N7: J1.pulse, Parte1.D3_PWM
  N8: hc-sr1.Trig, Parte1.A0
  N9: hc-sr1.Echo, Parte1.A1
  N10: Parte1.D10_PWM/SS, S1.IN4
  N11: Parte1.D11_PWM/MOSI, S1.IN3
  N12: Parte1.D12/MISO, S1.IN2
  N13: Parte1.D13/SCK, S1.IN1
  N14: Parte1.D0/RX, R10.Pin_0
  N15: Parte1.D1/TX, R9.Pin_1
  N16: Parte1.D5_PWM, S1.ENA
  N17: Parte1.D6_PWM, S1.ENB
  N18: R9.Pin_0, U3.GND
  N19: R10.Pin_1, U3.RXD
  N20: U3.VCC, U3.CH_PD

custom parts:
  H-Bridge with L298N: h-bridge
  ESP8266 WiFi Module: Generic WiFi Module based on the ESP8266 with onboard PCB antenna and UART communications
